// Logisim project div-mod.circ as structural Verilog: 3 circuits, main circuit div/mod
module div_mod (
  input  [7:0] y,
  input  [7:0] x,
  input  start,
  input  clk,
  output rdy,
  output [7:0] mod,
  output [7:0] div
);

  wire or_1_out;
  wire [7:0] adder_1_out, multiplexer_1_out, multiplexer_2_out, subtractor_1_out;

  // Probe on y
  // Probe on x
  Subtractor subtractor_1 (.a(mod), .b(y), .out(subtractor_1_out));  // open: bin, bout
  Multiplexer #(.width(8), .disabled(0), .enable("false")) multiplexer_1 (
    .in0(subtractor_1_out), .in1(x), .out(multiplexer_1_out), .sel(start));
  Adder adder_1 (.a(8'h1), .b(div), .out(adder_1_out));  // open: cin, cout
  Comparator #(.mode("unsigned")) comparator_1 (.a(mod), .b(y), .lt(rdy));  // open: gt, eq
  Multiplexer #(.width(8), .disabled(0), .enable("false")) multiplexer_2 (
    .in0(adder_1_out), .in1({8{1'b0}}), .out(multiplexer_2_out), .sel(start));
  or or_1 (or_1_out, ~rdy, start);  // OR_Gate
  Register #(.trigger("falling")) regMod (.D(multiplexer_1_out), .en(or_1_out), .Q(mod), .clk(clk));  // open: clr
  Register #(.trigger("falling")) regDiv (.D(multiplexer_2_out), .en(or_1_out), .Q(div), .clk(clk));  // open: clr
  // Probe on mod
  // Probe on div

  // Notes on the sheet:
  //   Leonardo Rikhardsson
  //   You can solve the problem with
  //   just this gates, but you can use
  //   other gates if your solution differs
  //   from mine
  //   Click in the clk input repeatedly
  //   why it is not working properly
  //   With the hand, manually enter the values of x and y
  //   Set the value of the clk input to 0 and start to 1
  //   Click on the clk input twice to start
  //   Now set the value of the start input to 0
  //   Study your circuit to understand
  //   when start is 1 or rdy is 0. In this way,
  //   the outputs will remain constant when
  //   Help: The contents of registers are only modified
  //   when the input 'en' is 1.  Set this input to 1
  //   the circuit is in standby mode (rdy is 1 and start is 0).
endmodule

module test (
);

  wire Clk_out, div_mod_1_rdy, tester_1_clk_out, tester_1_fail, tester_1_start, tester_1_success;
  wire [7:0] div_mod_1_div, div_mod_1_mod, tester_1_x, tester_1_y;

  // Probe on tester_1_x
  // Probe on tester_1_x
  // Probe on tester_1_y
  // Probe on tester_1_y
  Clock Clk (.out(Clk_out));
  div_mod div_mod_1 (
    .x(tester_1_x), .start(tester_1_start), .clk(tester_1_clk_out), .y(tester_1_y), .rdy(div_mod_1_rdy),
    .div(div_mod_1_div), .mod(div_mod_1_mod));
  tester tester_1 (
    .rdy(div_mod_1_rdy), .clk_in(Clk_out), .y(tester_1_y), .x(tester_1_x), .start(tester_1_start),
    .success(tester_1_success), .fail(tester_1_fail), .clk_out(tester_1_clk_out), .div(div_mod_1_div),
    .mod(div_mod_1_mod));
  LED led_1 (.in(tester_1_fail));
  LED led_2 (.in(tester_1_success));
  // Probe on div_mod_1_mod
  // Probe on div_mod_1_mod
  // Probe on div_mod_1_div
  // Probe on div_mod_1_div

  // Notes on the sheet:
  //   Your circuit doesn't work for those x and y
  //   Select the module finder
  //   and test your circuit with those x and y
  //   Red means failure:
  //   The output found
  //   is not correct
  //   Take note of x and y
  //   Green means success
  //   Your solution matches
  //   the full timing diagram
  //   Congratulations!
endmodule

module tester (
  input  rdy,
  input  clk_in,
  input  [7:0] div,
  input  [7:0] mod,
  output [7:0] y,
  output [7:0] x,
  output start,
  output success,
  output fail,
  output clk_out
);

  wire and_1_out, and_2_out, comparator_1_eq, comparator_2_eq, d_ff_1_q;
  wire [4:0] counter_1_q;
  wire [7:0] divRef, modRef;
  wire [23:0] rom_1_data;

  Pull_Resistor #(.pull(1)) pull_resistor_1 (.node(rdy));
  D_Flip_Flop #(.trigger("falling")) d_ff_1 (.clk(clk_in), .D(1'b1), .Q(d_ff_1_q));  // open: Qn, preset, en, reset
  Pull_Resistor #(.pull(1)) pull_resistor_2 (.node(div));
  Pull_Resistor #(.pull(1)) pull_resistor_3 (.node(mod));
  and and_1 (and_1_out, d_ff_1_q, rdy, ~fail, ~rom_1_data[12]);  // AND_Gate
  Counter #(.width(5), .max('h1f), .trigger("falling")) counter_1 (
    .count(and_1_out), .Q(counter_1_q), .clk(clk_in));  // open: load, D, carry, clr
  Comparator #(.mode("unsigned")) comparator_1 (.a(div), .b(divRef), .eq(comparator_1_eq));  // open: gt, lt
  Comparator #(.mode("unsigned")) comparator_2 (.a(mod), .b(modRef), .eq(comparator_2_eq));  // open: gt, lt
  and and_2 (and_2_out, comparator_1_eq, comparator_2_eq);
  ROM #(.addrWidth(5), .dataWidth(24)) rom_1 (
    .addr(counter_1_q), .data({rom_1_data[23:9], start, rom_1_data[7:0]}));  // open: sel
  ROM #(.addrWidth(3), .dataWidth(32)) rom_2 (.addr(rom_1_data[2:0]), .data({x, y, divRef, modRef}));  // open: sel
  and and_3 (success, rom_1_data[12], rdy, and_2_out);
  and and_4 (fail, rom_1_data[4], rdy, ~and_2_out);  // AND_Gate
  and and_5 (clk_out, ~fail, clk_in);  // AND_Gate

  // Notes on the sheet:
  //   found[16] success[12] start[8]  valid[4] ex[2-0] 
  //   contents of rom_1 (hex, n*v repeats v):
  //   0 100 10 10 101 11 11 11 102 12 103 13 104 14 105 15 1015 4*200015 201015
  //   contents of rom_2 (hex, n*v repeats v):
  //   1010100 2010200 3020101 11030502 5c120502 c51a070f
endmodule
